// Logisim project project.circ as structural Verilog
module asset_memory (
  input  [7:0] addr,
  input  colcell,
  input  clock,
  output [15:0] column,
  output \end 
);

  wire [2:0] rom_1_data;
  wire [3:0] counter_1_q;
  wire [15:0] multiplexer_1_out, multiplexer_3_out, multiplexer_4_out, multiplexer_5_out, multiplexer_6_out,
       multiplexer_7_out, multiplexer_8_out, multiplexer_9_out, multiplexer_10_out, multiplexer_11_out,
       multiplexer_12_out, multiplexer_13_out, multiplexer_14_out, multiplexer_15_out, multiplexer_16_out,
       multiplexer_17_out, multiplexer_18_out, multiplexer_19_out, multiplexer_20_out, multiplexer_21_out,
       multiplexer_22_out, multiplexer_23_out, multiplexer_24_out, multiplexer_25_out, multiplexer_26_out,
       multiplexer_27_out, multiplexer_28_out, multiplexer_29_out, multiplexer_30_out, multiplexer_31_out,
       multiplexer_32_out, multiplexer_33_out, multiplexer_34_out, multiplexer_35_out;

  Counter #(.width(4), .max('hf)) counter_1 (.Q(counter_1_q), .carry(\end ), .clk(clock));  // open: load, D, count, clr
  DotMatrix #(.matrixcols(16), .matrixrows(16)) dotmatrix_1 (
    .col0({16{1'b0}}), .col1({16{1'b0}}), .col2({16{1'b0}}), .col3({16{1'b0}}), .col4({16{1'b0}}),
    .col5({16{1'b0}}), .col6({16{1'b0}}), .col7({16{1'b0}}), .col8({16{1'b0}}), .col9({16{1'b0}}),
    .col10({16{1'b0}}), .col11({16{1'b0}}), .col12({16{1'b0}}), .col13({16{1'b0}}), .col14({16{1'b0}}),
    .col15({16{1'b0}}));
  DotMatrix #(.matrixcols(16), .matrixrows(16)) dotmatrix_2 (
    .col0({16{1'b0}}), .col1({16{1'b0}}), .col2({16{1'b0}}), .col3({16{1'b0}}), .col4(16'hc), .col5(16'hc34),
    .col6(16'h12c4), .col7(16'h2104), .col8(16'h2104), .col9(16'h12c4), .col10(16'hc34), .col11(16'hc),
    .col12({16{1'b0}}), .col13({16{1'b0}}), .col14({16{1'b0}}), .col15({16{1'b0}}));
  DotMatrix #(.matrixcols(16), .matrixrows(16)) dotmatrix_3 (
    .col0({16{1'b0}}), .col1({16{1'b0}}), .col2({16{1'b0}}), .col3(16'h300), .col4(16'h48c), .col5(16'h894),
    .col6(16'hd64), .col7(16'h31a4), .col8(16'h2024), .col9(16'h1024), .col10(16'h874), .col11(16'h78c),
    .col12({16{1'b0}}), .col13({16{1'b0}}), .col14({16{1'b0}}), .col15({16{1'b0}}));
  DotMatrix #(.matrixcols(16), .matrixrows(16)) dotmatrix_4 (
    .col0({16{1'b0}}), .col1({16{1'b0}}), .col2({16{1'b0}}), .col3(16'hc), .col4(16'h34), .col5(16'he54),
    .col6(16'h1394), .col7(16'h2414), .col8(16'h2814), .col9(16'h3394), .col10(16'he54), .col11(16'h34),
    .col12(16'hc), .col13({16{1'b0}}), .col14({16{1'b0}}), .col15({16{1'b0}}));
  DotMatrix #(.matrixcols(16), .matrixrows(16)) dotmatrix_5 (
    .col0({16{1'b0}}), .col1({16{1'b0}}), .col2({16{1'b0}}), .col3(16'hc), .col4(16'h1834), .col5(16'h27d4),
    .col6(16'h1414), .col7(16'h2414), .col8(16'h2414), .col9(16'h1414), .col10(16'h27d4), .col11(16'h1834),
    .col12(16'hc), .col13({16{1'b0}}), .col14({16{1'b0}}), .col15({16{1'b0}}));
  DotMatrix #(.matrixcols(16), .matrixrows(16)) dotmatrix_6 (
    .col0({16{1'b0}}), .col1({16{1'b0}}), .col2({16{1'b0}}), .col3(16'hf80), .col4(16'h44c), .col5(16'h234),
    .col6(16'h1414), .col7(16'h2814), .col8(16'h2814), .col9(16'h1414), .col10(16'h234), .col11(16'h44c),
    .col12(16'hf80), .col13({16{1'b0}}), .col14({16{1'b0}}), .col15({16{1'b0}}));
  DotMatrix #(.matrixcols(16), .matrixrows(16)) dotmatrix_7 (
    .col0({16{1'b0}}), .col1({16{1'b0}}), .col2(16'h780), .col3(16'h840), .col4(16'h92c), .col5(16'ha94),
    .col6(16'h1d94), .col7(16'h2014), .col8(16'h2014), .col9(16'h1d94), .col10(16'ha94), .col11(16'h92c),
    .col12(16'h840), .col13(16'h780), .col14({16{1'b0}}), .col15({16{1'b0}}));
  ROM #(.addrWidth(4), .dataWidth(3)) rom_1 (.addr(addr[3:0]), .data(rom_1_data));  // open: sel
  Multiplexer #(.width(16), .enable("false")) multiplexer_1 (
    .in0(multiplexer_4_out), .in1(multiplexer_19_out), .out(multiplexer_1_out), .sel(addr[5]));
  Multiplexer #(.width(16), .enable("false")) multiplexer_2 (
    .in0(multiplexer_1_out), .in1(multiplexer_3_out), .out(column), .sel(colcell));
  Multiplexer #(.width(16), .enable("false")) multiplexer_3 (
    .in0(multiplexer_27_out), .in1(multiplexer_35_out), .out(multiplexer_3_out), .sel(addr[5]));
  Multiplexer #(.select(3), .width(16), .enable("false")) multiplexer_4 (
    .in0(multiplexer_5_out), .in1(multiplexer_6_out), .in2(multiplexer_7_out), .in3(multiplexer_8_out),
    .in4(multiplexer_9_out), .in5(multiplexer_10_out), .in6(multiplexer_11_out), .out(multiplexer_4_out),
    .sel(rom_1_data));  // open: in7
  Multiplexer #(.select(4), .width(16), .enable("false")) multiplexer_5 (
    .in0({16{1'b0}}), .in1({16{1'b0}}), .in2({16{1'b0}}), .in3({16{1'b0}}), .in4({16{1'b0}}),
    .in5({16{1'b0}}), .in6({16{1'b0}}), .in7({16{1'b0}}), .in8({16{1'b0}}), .in9({16{1'b0}}),
    .in10({16{1'b0}}), .in11({16{1'b0}}), .in12({16{1'b0}}), .in13({16{1'b0}}), .in14({16{1'b0}}),
    .in15({16{1'b0}}), .out(multiplexer_5_out), .sel(counter_1_q));
  Multiplexer #(.select(4), .width(16), .enable("false")) multiplexer_6 (
    .in0({16{1'b0}}), .in1({16{1'b0}}), .in2({16{1'b0}}), .in3({16{1'b0}}), .in4(16'hc), .in5(16'hc34),
    .in6(16'h12c4), .in7(16'h2104), .in8(16'h2104), .in9(16'h12c4), .in10(16'hc34), .in11(16'hc),
    .in12({16{1'b0}}), .in13({16{1'b0}}), .in14({16{1'b0}}), .in15({16{1'b0}}), .out(multiplexer_6_out),
    .sel(counter_1_q));
  Multiplexer #(.select(4), .width(16), .enable("false")) multiplexer_7 (
    .in0({16{1'b0}}), .in1({16{1'b0}}), .in2({16{1'b0}}), .in3(16'h300), .in4(16'h48c), .in5(16'h894),
    .in6(16'hd64), .in7(16'h31a4), .in8(16'h2024), .in9(16'h1024), .in10(16'h874), .in11(16'h78c),
    .in12({16{1'b0}}), .in13({16{1'b0}}), .in14({16{1'b0}}), .in15({16{1'b0}}), .out(multiplexer_7_out),
    .sel(counter_1_q));
  Multiplexer #(.select(4), .width(16), .enable("false")) multiplexer_8 (
    .in0({16{1'b0}}), .in1({16{1'b0}}), .in2({16{1'b0}}), .in3(16'hc), .in4(16'h34), .in5(16'he54),
    .in6(16'h1394), .in7(16'h2414), .in8(16'h2814), .in9(16'h3394), .in10(16'he54), .in11(16'h34),
    .in12(16'hc), .in13({16{1'b0}}), .in14({16{1'b0}}), .in15({16{1'b0}}), .out(multiplexer_8_out),
    .sel(counter_1_q));
  Multiplexer #(.select(4), .width(16), .enable("false")) multiplexer_9 (
    .in0({16{1'b0}}), .in1({16{1'b0}}), .in2({16{1'b0}}), .in3(16'hc), .in4(16'h1834), .in5(16'h27d4),
    .in6(16'h1414), .in7(16'h2414), .in8(16'h2414), .in9(16'h1414), .in10(16'h27d4), .in11(16'h1834),
    .in12(16'hc), .in13({16{1'b0}}), .in14({16{1'b0}}), .in15({16{1'b0}}), .out(multiplexer_9_out),
    .sel(counter_1_q));
  Multiplexer #(.select(4), .width(16), .enable("false")) multiplexer_10 (
    .in0({16{1'b0}}), .in1({16{1'b0}}), .in2({16{1'b0}}), .in3(16'hf80), .in4(16'h44c), .in5(16'h234),
    .in6(16'h1414), .in7(16'h2814), .in8(16'h2814), .in9(16'h1414), .in10(16'h234), .in11(16'h44c),
    .in12(16'hf80), .in13({16{1'b0}}), .in14({16{1'b0}}), .in15({16{1'b0}}), .out(multiplexer_10_out),
    .sel(counter_1_q));
  Multiplexer #(.select(4), .width(16), .enable("false")) multiplexer_11 (
    .in0({16{1'b0}}), .in1({16{1'b0}}), .in2(16'h780), .in3(16'h840), .in4(16'h92c), .in5(16'ha94),
    .in6(16'h1d94), .in7(16'h2014), .in8(16'h2014), .in9(16'h1d94), .in10(16'ha94), .in11(16'h92c),
    .in12(16'h840), .in13(16'h780), .in14({16{1'b0}}), .in15({16{1'b0}}), .out(multiplexer_11_out),
    .sel(counter_1_q));
  DotMatrix #(.matrixcols(16), .matrixrows(16)) dotmatrix_8 (
    .col0({16{1'b0}}), .col1({16{1'b0}}), .col2({16{1'b0}}), .col3({16{1'b0}}), .col4({16{1'b0}}),
    .col5({16{1'b0}}), .col6({16{1'b0}}), .col7({16{1'b0}}), .col8({16{1'b0}}), .col9({16{1'b0}}),
    .col10({16{1'b0}}), .col11({16{1'b0}}), .col12({16{1'b0}}), .col13({16{1'b0}}), .col14({16{1'b0}}),
    .col15({16{1'b0}}));
  DotMatrix #(.matrixcols(16), .matrixrows(16)) dotmatrix_9 (
    .col0({16{1'b0}}), .col1({16{1'b0}}), .col2({16{1'b0}}), .col3(16'hc), .col4(16'hc32), .col5(16'h12ca),
    .col6(16'h2d3a), .col7(16'h5efa), .col8(16'h5efa), .col9(16'h2d3a), .col10(16'h12ca), .col11(16'hc32),
    .col12(16'hc), .col13({16{1'b0}}), .col14({16{1'b0}}), .col15({16{1'b0}}));
  DotMatrix #(.matrixcols(16), .matrixrows(16)) dotmatrix_10 (
    .col0({16{1'b0}}), .col1({16{1'b0}}), .col2(16'h300), .col3(16'h48c), .col4(16'hb52), .col5(16'h176a),
    .col6(16'h329a), .col7(16'h4e5a), .col8(16'h5fda), .col9(16'h2fda), .col10(16'h178a), .col11(16'h872),
    .col12(16'h78c), .col13({16{1'b0}}), .col14({16{1'b0}}), .col15({16{1'b0}}));
  DotMatrix #(.matrixcols(16), .matrixrows(16)) dotmatrix_11 (
    .col0({16{1'b0}}), .col1({16{1'b0}}), .col2(16'hc), .col3(16'h32), .col4(16'he4a), .col5(16'h11aa),
    .col6(16'h2c6a), .col7(16'h5bea), .col8(16'h57ea), .col9(16'h4c6a), .col10(16'h31aa), .col11(16'he4a),
    .col12(16'h32), .col13(16'hc), .col14({16{1'b0}}), .col15({16{1'b0}}));
  DotMatrix #(.matrixcols(16), .matrixrows(16)) dotmatrix_12 (
    .col0({16{1'b0}}), .col1({16{1'b0}}), .col2(16'hc), .col3(16'h1832), .col4(16'h27ca), .col5(16'h582a),
    .col6(16'h6bea), .col7(16'h5bea), .col8(16'h5bea), .col9(16'h6bea), .col10(16'h582a), .col11(16'h27ca),
    .col12(16'h1832), .col13(16'hc), .col14({16{1'b0}}), .col15({16{1'b0}}));
  DotMatrix #(.matrixcols(16), .matrixrows(16)) dotmatrix_13 (
    .col0({16{1'b0}}), .col1({16{1'b0}}), .col2(16'hf80), .col3(16'h104c), .col4(16'hbb2), .col5(16'h1dca),
    .col6(16'h2bea), .col7(16'h57ea), .col8(16'h57ea), .col9(16'h2bea), .col10(16'h1dca), .col11(16'hbb2),
    .col12(16'h104c), .col13(16'hf80), .col14({16{1'b0}}), .col15({16{1'b0}}));
  DotMatrix #(.matrixcols(16), .matrixrows(16)) dotmatrix_14 (
    .col0({16{1'b0}}), .col1(16'h780), .col2(16'h840), .col3(16'h17ac), .col4(16'h16d2), .col5(16'h156a),
    .col6(16'h226a), .col7(16'h5fea), .col8(16'h5fea), .col9(16'h226a), .col10(16'h156a), .col11(16'h16d2),
    .col12(16'h17ac), .col13(16'h840), .col14(16'h780), .col15({16{1'b0}}));
  Multiplexer #(.select(4), .width(16), .enable("false")) multiplexer_12 (
    .in0({16{1'b0}}), .in1({16{1'b0}}), .in2({16{1'b0}}), .in3({16{1'b0}}), .in4({16{1'b0}}),
    .in5({16{1'b0}}), .in6({16{1'b0}}), .in7({16{1'b0}}), .in8({16{1'b0}}), .in9({16{1'b0}}),
    .in10({16{1'b0}}), .in11({16{1'b0}}), .in12({16{1'b0}}), .in13({16{1'b0}}), .in14({16{1'b0}}),
    .in15({16{1'b0}}), .out(multiplexer_12_out), .sel(counter_1_q));
  Multiplexer #(.select(4), .width(16), .enable("false")) multiplexer_13 (
    .in0({16{1'b0}}), .in1({16{1'b0}}), .in2({16{1'b0}}), .in3(16'hc), .in4(16'hc32), .in5(16'h12ca),
    .in6(16'h2d3a), .in7(16'h5efa), .in8(16'h5efa), .in9(16'h2d3a), .in10(16'h12ca), .in11(16'hc32),
    .in12(16'hc), .in13({16{1'b0}}), .in14({16{1'b0}}), .in15({16{1'b0}}), .out(multiplexer_13_out),
    .sel(counter_1_q));
  Multiplexer #(.select(4), .width(16), .enable("false")) multiplexer_14 (
    .in0({16{1'b0}}), .in1({16{1'b0}}), .in2(16'h300), .in3(16'h48c), .in4(16'hb52), .in5(16'h176a),
    .in6(16'h329a), .in7(16'h4e5a), .in8(16'h5fda), .in9(16'h2fda), .in10(16'h178a), .in11(16'h872),
    .in12(16'h78c), .in13({16{1'b0}}), .in14({16{1'b0}}), .in15({16{1'b0}}), .out(multiplexer_14_out),
    .sel(counter_1_q));
  Multiplexer #(.select(4), .width(16), .enable("false")) multiplexer_15 (
    .in0({16{1'b0}}), .in1({16{1'b0}}), .in2(16'hc), .in3(16'h32), .in4(16'he4a), .in5(16'h11aa),
    .in6(16'h2c6a), .in7(16'h5bea), .in8(16'h57ea), .in9(16'h4c6a), .in10(16'h31aa), .in11(16'he4a),
    .in12(16'h32), .in13(16'hc), .in14({16{1'b0}}), .in15({16{1'b0}}), .out(multiplexer_15_out),
    .sel(counter_1_q));
  Multiplexer #(.select(4), .width(16), .enable("false")) multiplexer_16 (
    .in0({16{1'b0}}), .in1({16{1'b0}}), .in2(16'hc), .in3(16'h1832), .in4(16'h27ca), .in5(16'h582a),
    .in6(16'h6bea), .in7(16'h5bea), .in8(16'h5bea), .in9(16'h6bea), .in10(16'h582a), .in11(16'h27ca),
    .in12(16'h1832), .in13(16'hc), .in14({16{1'b0}}), .in15({16{1'b0}}), .out(multiplexer_16_out),
    .sel(counter_1_q));
  Multiplexer #(.select(4), .width(16), .enable("false")) multiplexer_17 (
    .in0({16{1'b0}}), .in1({16{1'b0}}), .in2(16'hf80), .in3(16'h104c), .in4(16'hbb2), .in5(16'h1dca),
    .in6(16'h2bea), .in7(16'h57ea), .in8(16'h57ea), .in9(16'h2bea), .in10(16'h1dca), .in11(16'hbb2),
    .in12(16'h104c), .in13(16'hf80), .in14({16{1'b0}}), .in15({16{1'b0}}), .out(multiplexer_17_out),
    .sel(counter_1_q));
  Multiplexer #(.select(4), .width(16), .enable("false")) multiplexer_18 (
    .in0({16{1'b0}}), .in1(16'h780), .in2(16'h840), .in3(16'h17ac), .in4(16'h16d2), .in5(16'h156a),
    .in6(16'h226a), .in7(16'h5fea), .in8(16'h5fea), .in9(16'h226a), .in10(16'h156a), .in11(16'h16d2),
    .in12(16'h17ac), .in13(16'h840), .in14(16'h780), .in15({16{1'b0}}), .out(multiplexer_18_out),
    .sel(counter_1_q));
  Multiplexer #(.select(3), .width(16), .enable("false")) multiplexer_19 (
    .in0(multiplexer_12_out), .in1(multiplexer_13_out), .in2(multiplexer_14_out), .in3(multiplexer_15_out),
    .in4(multiplexer_16_out), .in5(multiplexer_17_out), .in6(multiplexer_18_out), .out(multiplexer_19_out),
    .sel(rom_1_data));  // open: in7
  DotMatrix #(.matrixcols(16), .matrixrows(16)) dotmatrix_15 (
    .col0({16{1'b1}}), .col1({16{1'b1}}), .col2({16{1'b1}}), .col3({16{1'b1}}), .col4({16{1'b1}}),
    .col5({16{1'b1}}), .col6({16{1'b1}}), .col7({16{1'b1}}), .col8({16{1'b1}}), .col9({16{1'b1}}),
    .col10({16{1'b1}}), .col11({16{1'b1}}), .col12({16{1'b1}}), .col13({16{1'b1}}), .col14({16{1'b1}}),
    .col15({16{1'b1}}));
  DotMatrix #(.matrixcols(16), .matrixrows(16)) dotmatrix_16 (
    .col0({16{1'b1}}), .col1({16{1'b1}}), .col2({16{1'b1}}), .col3(16'hfff3), .col4(16'hf3cd),
    .col5(16'hed35), .col6(16'hd2c5), .col7(16'ha105), .col8(16'ha105), .col9(16'hd2c5), .col10(16'hed35),
    .col11(16'hf3cd), .col12(16'hfff3), .col13({16{1'b1}}), .col14({16{1'b1}}), .col15({16{1'b1}}));
  DotMatrix #(.matrixcols(16), .matrixrows(16)) dotmatrix_17 (
    .col0({16{1'b1}}), .col1({16{1'b1}}), .col2(16'hfcff), .col3(16'hfb73), .col4(16'hf4ad), .col5(16'he895),
    .col6(16'hcd65), .col7(16'hb1a5), .col8(16'ha025), .col9(16'hd025), .col10(16'he875), .col11(16'hf78d),
    .col12(16'hf873), .col13({16{1'b1}}), .col14({16{1'b1}}), .col15({16{1'b1}}));
  DotMatrix #(.matrixcols(16), .matrixrows(16)) dotmatrix_18 (
    .col0({16{1'b1}}), .col1({16{1'b1}}), .col2(16'hfff3), .col3(16'hffcd), .col4(16'hf1b5), .col5(16'hee55),
    .col6(16'hd395), .col7(16'ha415), .col8(16'ha815), .col9(16'hb395), .col10(16'hce55), .col11(16'hf1b5),
    .col12(16'hffcd), .col13(16'hfff3), .col14({16{1'b1}}), .col15({16{1'b1}}));
  DotMatrix #(.matrixcols(16), .matrixrows(16)) dotmatrix_19 (
    .col0({16{1'b1}}), .col1({16{1'b1}}), .col2(16'hfff3), .col3(16'he7cd), .col4(16'hd835), .col5(16'ha7d5),
    .col6(16'h9415), .col7(16'ha415), .col8(16'ha415), .col9(16'h9415), .col10(16'ha7d5), .col11(16'hd835),
    .col12(16'he7cd), .col13(16'hfff3), .col14({16{1'b1}}), .col15({16{1'b1}}));
  DotMatrix #(.matrixcols(16), .matrixrows(16)) dotmatrix_20 (
    .col0({16{1'b1}}), .col1({16{1'b1}}), .col2(16'hf07f), .col3(16'hefb3), .col4(16'hf44d), .col5(16'he235),
    .col6(16'hd415), .col7(16'ha815), .col8(16'ha815), .col9(16'hd415), .col10(16'he235), .col11(16'hf44d),
    .col12(16'hefb3), .col13(16'hf07f), .col14({16{1'b1}}), .col15({16{1'b1}}));
  DotMatrix #(.matrixcols(16), .matrixrows(16)) dotmatrix_21 (
    .col0({16{1'b1}}), .col1(16'hf87f), .col2(16'hf7bf), .col3(16'he853), .col4(16'he92d), .col5(16'hea95),
    .col6(16'hdd95), .col7(16'ha015), .col8(16'ha015), .col9(16'hdd95), .col10(16'hea95), .col11(16'he92d),
    .col12(16'he853), .col13(16'hf7bf), .col14(16'hf87f), .col15({16{1'b1}}));
  Multiplexer #(.select(4), .width(16), .enable("false")) multiplexer_20 (
    .in0({16{1'b1}}), .in1({16{1'b1}}), .in2({16{1'b1}}), .in3({16{1'b1}}), .in4({16{1'b1}}),
    .in5({16{1'b1}}), .in6({16{1'b1}}), .in7({16{1'b1}}), .in8({16{1'b1}}), .in9({16{1'b1}}),
    .in10({16{1'b1}}), .in11({16{1'b1}}), .in12({16{1'b1}}), .in13({16{1'b1}}), .in14({16{1'b1}}),
    .in15({16{1'b1}}), .out(multiplexer_20_out), .sel(counter_1_q));
  Multiplexer #(.select(4), .width(16), .enable("false")) multiplexer_21 (
    .in0({16{1'b1}}), .in1({16{1'b1}}), .in2({16{1'b1}}), .in3(16'hfff3), .in4(16'hf3cd), .in5(16'hed35),
    .in6(16'hd2c5), .in7(16'ha105), .in8(16'ha105), .in9(16'hd2c5), .in10(16'hed35), .in11(16'hf3cd),
    .in12(16'hfff3), .in13({16{1'b1}}), .in14({16{1'b1}}), .in15({16{1'b1}}), .out(multiplexer_21_out),
    .sel(counter_1_q));
  Multiplexer #(.select(4), .width(16), .enable("false")) multiplexer_22 (
    .in0({16{1'b1}}), .in1({16{1'b1}}), .in2(16'hfcff), .in3(16'hfb73), .in4(16'hf4ad), .in5(16'he895),
    .in6(16'hcd65), .in7(16'hb1a5), .in8(16'ha025), .in9(16'hd025), .in10(16'he875), .in11(16'hf78d),
    .in12(16'hf873), .in13({16{1'b1}}), .in14({16{1'b1}}), .in15({16{1'b1}}), .out(multiplexer_22_out),
    .sel(counter_1_q));
  Multiplexer #(.select(4), .width(16), .enable("false")) multiplexer_23 (
    .in0({16{1'b1}}), .in1({16{1'b1}}), .in2(16'hfff3), .in3(16'hffcd), .in4(16'hf1b5), .in5(16'hee55),
    .in6(16'hd395), .in7(16'ha415), .in8(16'ha815), .in9(16'hb395), .in10(16'hce55), .in11(16'hf1b5),
    .in12(16'hffcd), .in13(16'hfff3), .in14({16{1'b1}}), .in15({16{1'b1}}), .out(multiplexer_23_out),
    .sel(counter_1_q));
  Multiplexer #(.select(4), .width(16), .enable("false")) multiplexer_24 (
    .in0({16{1'b1}}), .in1({16{1'b1}}), .in2(16'hfff3), .in3(16'he7cd), .in4(16'hd835), .in5(16'ha7d5),
    .in6(16'h9415), .in7(16'ha415), .in8(16'ha415), .in9(16'h9415), .in10(16'ha7d5), .in11(16'hd835),
    .in12(16'he7cd), .in13(16'hfff3), .in14({16{1'b1}}), .in15({16{1'b1}}), .out(multiplexer_24_out),
    .sel(counter_1_q));
  Multiplexer #(.select(4), .width(16), .enable("false")) multiplexer_25 (
    .in0({16{1'b1}}), .in1({16{1'b1}}), .in2(16'hf07f), .in3(16'hefb3), .in4(16'hf44d), .in5(16'he235),
    .in6(16'hd415), .in7(16'ha815), .in8(16'ha815), .in9(16'hd415), .in10(16'he235), .in11(16'hf44d),
    .in12(16'hefb3), .in13(16'hf07f), .in14({16{1'b1}}), .in15({16{1'b1}}), .out(multiplexer_25_out),
    .sel(counter_1_q));
  Multiplexer #(.select(4), .width(16), .enable("false")) multiplexer_26 (
    .in0({16{1'b1}}), .in1(16'hf87f), .in2(16'hf7bf), .in3(16'he853), .in4(16'he92d), .in5(16'hea95),
    .in6(16'hdd95), .in7(16'ha015), .in8(16'ha015), .in9(16'hdd95), .in10(16'hea95), .in11(16'he92d),
    .in12(16'he853), .in13(16'hf7bf), .in14(16'hf87f), .in15({16{1'b1}}), .out(multiplexer_26_out),
    .sel(counter_1_q));
  Multiplexer #(.select(3), .width(16), .enable("false")) multiplexer_27 (
    .in0(multiplexer_20_out), .in1(multiplexer_21_out), .in2(multiplexer_22_out), .in3(multiplexer_23_out),
    .in4(multiplexer_24_out), .in5(multiplexer_25_out), .in6(multiplexer_26_out), .out(multiplexer_27_out),
    .sel(rom_1_data));  // open: in7
  DotMatrix #(.matrixcols(16), .matrixrows(16)) dotmatrix_22 (
    .col0({16{1'b1}}), .col1({16{1'b1}}), .col2({16{1'b1}}), .col3({16{1'b1}}), .col4({16{1'b1}}),
    .col5({16{1'b1}}), .col6({16{1'b1}}), .col7({16{1'b1}}), .col8({16{1'b1}}), .col9({16{1'b1}}),
    .col10({16{1'b1}}), .col11({16{1'b1}}), .col12({16{1'b1}}), .col13({16{1'b1}}), .col14({16{1'b1}}),
    .col15({16{1'b1}}));
  DotMatrix #(.matrixcols(16), .matrixrows(16)) dotmatrix_23 (
    .col0({16{1'b1}}), .col1({16{1'b1}}), .col2({16{1'b1}}), .col3({16{1'b1}}), .col4(16'hfff3),
    .col5(16'hf3cb), .col6(16'hed3b), .col7(16'hdefb), .col8(16'hdefb), .col9(16'hed3b), .col10(16'hf3cb),
    .col11(16'hfff3), .col12({16{1'b1}}), .col13({16{1'b1}}), .col14({16{1'b1}}), .col15({16{1'b1}}));
  DotMatrix #(.matrixcols(16), .matrixrows(16)) dotmatrix_24 (
    .col0({16{1'b1}}), .col1({16{1'b1}}), .col2({16{1'b1}}), .col3(16'hfcff), .col4(16'hfb73),
    .col5(16'hf76b), .col6(16'hf29b), .col7(16'hce5b), .col8(16'hdfdb), .col9(16'hefdb), .col10(16'hf78b),
    .col11(16'hf873), .col12({16{1'b1}}), .col13({16{1'b1}}), .col14({16{1'b1}}), .col15({16{1'b1}}));
  DotMatrix #(.matrixcols(16), .matrixrows(16)) dotmatrix_25 (
    .col0({16{1'b1}}), .col1({16{1'b1}}), .col2({16{1'b1}}), .col3(16'hfff3), .col4(16'hffcb),
    .col5(16'hf1ab), .col6(16'hec6b), .col7(16'hdbeb), .col8(16'hd7eb), .col9(16'hcc6b), .col10(16'hf1ab),
    .col11(16'hffcb), .col12(16'hfff3), .col13({16{1'b1}}), .col14({16{1'b1}}), .col15({16{1'b1}}));
  DotMatrix #(.matrixcols(16), .matrixrows(16)) dotmatrix_26 (
    .col0({16{1'b1}}), .col1({16{1'b1}}), .col2({16{1'b1}}), .col3(16'hfff3), .col4(16'he7cb),
    .col5(16'hd82b), .col6(16'hebeb), .col7(16'hdbeb), .col8(16'hdbeb), .col9(16'hebeb), .col10(16'hd82b),
    .col11(16'he7cb), .col12(16'hfff3), .col13({16{1'b1}}), .col14({16{1'b1}}), .col15({16{1'b1}}));
  DotMatrix #(.matrixcols(16), .matrixrows(16)) dotmatrix_27 (
    .col0({16{1'b1}}), .col1({16{1'b1}}), .col2({16{1'b1}}), .col3(16'hf07f), .col4(16'hfbb3),
    .col5(16'hfdcb), .col6(16'hebeb), .col7(16'hd7eb), .col8(16'hd7eb), .col9(16'hebeb), .col10(16'hfdcb),
    .col11(16'hfbb3), .col12(16'hf07f), .col13({16{1'b1}}), .col14({16{1'b1}}), .col15({16{1'b1}}));
  DotMatrix #(.matrixcols(16), .matrixrows(16)) dotmatrix_28 (
    .col0({16{1'b1}}), .col1({16{1'b1}}), .col2(16'hf87f), .col3(16'hf7bf), .col4(16'hf6d3), .col5(16'hf56b),
    .col6(16'he26b), .col7(16'hdfeb), .col8(16'hdfeb), .col9(16'he26b), .col10(16'hf56b), .col11(16'hf6d3),
    .col12(16'hf7bf), .col13(16'hf87f), .col14({16{1'b1}}), .col15({16{1'b1}}));
  Multiplexer #(.select(4), .width(16), .enable("false")) multiplexer_28 (
    .in0({16{1'b1}}), .in1({16{1'b1}}), .in2({16{1'b1}}), .in3({16{1'b1}}), .in4({16{1'b1}}),
    .in5({16{1'b1}}), .in6({16{1'b1}}), .in7({16{1'b1}}), .in8({16{1'b1}}), .in9({16{1'b1}}),
    .in10({16{1'b1}}), .in11({16{1'b1}}), .in12({16{1'b1}}), .in13({16{1'b1}}), .in14({16{1'b1}}),
    .in15({16{1'b1}}), .out(multiplexer_28_out), .sel(counter_1_q));
  Multiplexer #(.select(4), .width(16), .enable("false")) multiplexer_29 (
    .in0({16{1'b1}}), .in1({16{1'b1}}), .in2({16{1'b1}}), .in3({16{1'b1}}), .in4(16'hfff3), .in5(16'hf3cb),
    .in6(16'hed3b), .in7(16'hdefb), .in8(16'hdefb), .in9(16'hed3b), .in10(16'hf3cb), .in11(16'hfff3),
    .in12({16{1'b1}}), .in13({16{1'b1}}), .in14({16{1'b1}}), .in15({16{1'b1}}), .out(multiplexer_29_out),
    .sel(counter_1_q));
  Multiplexer #(.select(4), .width(16), .enable("false")) multiplexer_30 (
    .in0({16{1'b1}}), .in1({16{1'b1}}), .in2({16{1'b1}}), .in3(16'hfcff), .in4(16'hfb73), .in5(16'hf76b),
    .in6(16'hf29b), .in7(16'hce5b), .in8(16'hdfdb), .in9(16'hefdb), .in10(16'hf78b), .in11(16'hf873),
    .in12({16{1'b1}}), .in13({16{1'b1}}), .in14({16{1'b1}}), .in15({16{1'b1}}), .out(multiplexer_30_out),
    .sel(counter_1_q));
  Multiplexer #(.select(4), .width(16), .enable("false")) multiplexer_31 (
    .in0({16{1'b1}}), .in1({16{1'b1}}), .in2({16{1'b1}}), .in3(16'hfff3), .in4(16'hffcb), .in5(16'hf1ab),
    .in6(16'hec6b), .in7(16'hdbeb), .in8(16'hd7eb), .in9(16'hcc6b), .in10(16'hf1ab), .in11(16'hffcb),
    .in12(16'hfff3), .in13({16{1'b1}}), .in14({16{1'b1}}), .in15({16{1'b1}}), .out(multiplexer_31_out),
    .sel(counter_1_q));
  Multiplexer #(.select(4), .width(16), .enable("false")) multiplexer_32 (
    .in0({16{1'b1}}), .in1({16{1'b1}}), .in2({16{1'b1}}), .in3(16'hfff3), .in4(16'he7cb), .in5(16'hd82b),
    .in6(16'hebeb), .in7(16'hdbeb), .in8(16'hdbeb), .in9(16'hebeb), .in10(16'hd82b), .in11(16'he7cb),
    .in12(16'hfff3), .in13({16{1'b1}}), .in14({16{1'b1}}), .in15({16{1'b1}}), .out(multiplexer_32_out),
    .sel(counter_1_q));
  Multiplexer #(.select(4), .width(16), .enable("false")) multiplexer_33 (
    .in0({16{1'b1}}), .in1({16{1'b1}}), .in2({16{1'b1}}), .in3(16'hf07f), .in4(16'hfbb3), .in5(16'hfdcb),
    .in6(16'hebeb), .in7(16'hd7eb), .in8(16'hd7eb), .in9(16'hebeb), .in10(16'hfdcb), .in11(16'hfbb3),
    .in12(16'hf07f), .in13({16{1'b1}}), .in14({16{1'b1}}), .in15({16{1'b1}}), .out(multiplexer_33_out),
    .sel(counter_1_q));
  Multiplexer #(.select(4), .width(16), .enable("false")) multiplexer_34 (
    .in0({16{1'b1}}), .in1({16{1'b1}}), .in2(16'hf87f), .in3(16'hf7bf), .in4(16'hf6d3), .in5(16'hf56b),
    .in6(16'he26b), .in7(16'hdfeb), .in8(16'hdfeb), .in9(16'he26b), .in10(16'hf56b), .in11(16'hf6d3),
    .in12(16'hf7bf), .in13(16'hf87f), .in14({16{1'b1}}), .in15({16{1'b1}}), .out(multiplexer_34_out),
    .sel(counter_1_q));
  Multiplexer #(.select(3), .width(16), .enable("false")) multiplexer_35 (
    .in0(multiplexer_28_out), .in1(multiplexer_29_out), .in2(multiplexer_30_out), .in3(multiplexer_31_out),
    .in4(multiplexer_32_out), .in5(multiplexer_33_out), .in6(multiplexer_34_out), .out(multiplexer_35_out),
    .sel(rom_1_data));  // open: in7

  // Notes on the sheet:
  //   contents of rom_1 (hex, n*v repeats v):
  //   6*0 3 0 6 0 0 5 0 4 2 1
endmodule

module matrix16x16 (
  input  [15:0] column,
  input  clk,
  input  res,
  input  [3:0] current_column,
  input  change_matrix,
  output [15:0] column_2,
  output [15:0] column_4,
  output [15:0] column_6,
  output [15:0] column_8,
  output [15:0] column_10,
  output [15:0] column_12,
  output [15:0] column_14,
  output [15:0] column_16,
  output [15:0] column_1,
  output [15:0] column_3,
  output [15:0] column_5,
  output [15:0] column_7,
  output [15:0] column_9,
  output [15:0] column_11,
  output [15:0] column_13,
  output [15:0] column_15
);

  wire controlled_buffer_2_out, decoder_1_out0, decoder_1_out1, decoder_1_out2, decoder_1_out3,
       decoder_1_out4, decoder_1_out5, decoder_1_out6, decoder_1_out7, decoder_1_out8, decoder_1_out9,
       decoder_1_out10, decoder_1_out11, undriven;
  wire [3:0] controlled_buffer_1_out;

  Register #(.width(16)) register_1 (.D(column), .Q(column_1));  // open: en, clk, clr
  Register #(.width(16)) register_2 (.D(column), .Q(column_2));  // open: en, clk, clr
  Register #(.width(16)) register_3 (
    .D(column), .en(decoder_1_out1), .Q(column_4), .clk(clk), .clr(controlled_buffer_2_out));
  Register #(.width(16)) register_4 (
    .D(column), .en(decoder_1_out0), .Q(column_3), .clk(clk), .clr(controlled_buffer_2_out));
  Register #(.width(16)) register_5 (
    .D(column), .en(decoder_1_out2), .Q(column_5), .clk(clk), .clr(controlled_buffer_2_out));
  assign controlled_buffer_1_out = change_matrix ? current_column : 4'bz;  // Controlled_Buffer controlled_buffer_1
  Decoder #(.select(4), .disabled(0)) decoder_1 (
    .out0(decoder_1_out0), .out1(decoder_1_out1), .out2(decoder_1_out2), .out3(decoder_1_out3),
    .out4(decoder_1_out4), .out5(decoder_1_out5), .out6(decoder_1_out6), .out7(decoder_1_out7),
    .out8(decoder_1_out8), .out9(decoder_1_out9), .out10(decoder_1_out10), .out11(decoder_1_out11),
    .sel(controlled_buffer_1_out), .en(change_matrix));  // open: out12, out13, out14, out15
  Register #(.width(16)) register_6 (
    .D(column), .en(decoder_1_out3), .Q(column_6), .clk(clk), .clr(controlled_buffer_2_out));
  Register #(.width(16)) register_7 (
    .D(column), .en(decoder_1_out4), .Q(column_7), .clk(clk), .clr(controlled_buffer_2_out));
  Register #(.width(16)) register_8 (
    .D(column), .en(decoder_1_out5), .Q(column_8), .clk(clk), .clr(controlled_buffer_2_out));
  Register #(.width(16)) register_9 (
    .D(column), .en(decoder_1_out6), .Q(column_9), .clk(clk), .clr(controlled_buffer_2_out));
  Register #(.width(16)) register_10 (
    .D(column), .en(decoder_1_out7), .Q(column_10), .clk(clk), .clr(controlled_buffer_2_out));
  Register #(.width(16)) register_11 (
    .D(column), .en(decoder_1_out8), .Q(column_11), .clk(clk), .clr(controlled_buffer_2_out));
  Register #(.width(16)) register_12 (
    .D(column), .en(decoder_1_out9), .Q(column_12), .clk(clk), .clr(controlled_buffer_2_out));
  Register #(.width(16)) register_13 (
    .D(column), .en(decoder_1_out10), .Q(column_13), .clk(clk), .clr(controlled_buffer_2_out));
  Register #(.width(16)) register_14 (
    .D(column), .en(decoder_1_out11), .Q(column_14), .clk(clk), .clr(controlled_buffer_2_out));
  assign controlled_buffer_2_out = change_matrix ? res : 1'bz;  // Controlled_Buffer controlled_buffer_2
  Register #(.width(16)) register_15 (.D(column), .en(undriven), .Q(column_16));  // open: clk, clr
  Register #(.width(16)) register_16 (.D(column), .Q(column_15));  // open: en, clk, clr

  // Other names for the same wires on the sheet: cng_mtrx = change_matrix
endmodule
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